# Fritzing sketch ACS712 (saved by Fritzing 0.8.7b)

parts:
  U2 = ESP8266 NodeMCU LoLin module
  Componente1 = Current Sensor 5A
  R1 = Resistor [tolerance=±5% resistance=10k package=THT]
  R2 = Resistor [tolerance=±5% resistance=2.50 package=THT]

nets:
  VIN: U2.Vin, Componente1.VCC
  GND: U2.GND, U2.A0, Componente1.GND, R1.Pin_0, R2.Pin_0, R2.Pin_1
  N1: Componente1.OUT, R1.Pin_1

notes:
  2.5kΩ
  10kΩ

custom parts:
  ESP8266 NodeMCU LoLin module: ESP8266 based NodeMCU
